# Fritzing sketch plantuino (saved by Fritzing 0.9.10b)
breadboards: 1

parts:
  Bauteil1 = Arduino Uno (Rev3)
  LCD1 = LCD screen
  R1 = Resistor [tolerance=±5% resistance=220 package="2010 [SMD]"]
  Capacitive_Soil_Moisture_Sensor1 = DFRobot Capacitive Soil Moisture Sensor V1.0 [part_number=SEN0193]

nets:
  N1: Bauteil1.A0, Capacitive_Soil_Moisture_Sensor1.A
  N2: Bauteil1.D11_PWM/MOSI, LCD1.E
  N3: Bauteil1.D12/MISO, LCD1.RS
  N4: Bauteil1.D2, LCD1.DB7
  N5: Bauteil1.D3_PWM, LCD1.DB6
  N6: Bauteil1.D4, LCD1.DB5
  N7: Bauteil1.D5_PWM, LCD1.DB4
  N8: Bauteil1.D6_PWM, LCD1.V0
  5V: Bauteil1.5V, LCD1.VDD, R1.Pin_1, Capacitive_Soil_Moisture_Sensor1.VCC
  GND: Bauteil1.GND, LCD1.VSS, LCD1.R/W, LCD1.LED-, Capacitive_Soil_Moisture_Sensor1.GND
  N9: LCD1.LED+, R1.Pin_0

custom parts:
  DFRobot Capacitive Soil Moisture Sensor V1.0: DFRobot Capacitive Soil Moisture Sensor V1.0 This product measures soil moisture levels by capacitive sensing, rather than resistive sensing like other types of moisture sensor. It is made of a corrosion resistant material giving it a long service life. Insert it into soil and impress your friends with the real-time soil moisture data! The product includes an on-board voltage regulator which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
